# Fritzing sketch Plaque chauffante (saved by Fritzing 0.9.3b)
perfboards: 1

parts:
  Composant1 = Bluetooth HC-05 Macho
  Composant2 = Arduino Uno (Rev3)
  VCC1 = Battery  # not connected
  U1 = Voltage Regulator - 5V [package="TO220 [THT]"]
  J1 = Basic Force Sensing Resistor (FSR) [package=THT]
  T1 = LM35 Temperature Sensor [package="TO92 [THT]"]
  S1 = SPST Switch [package=r_sw_th]  # not connected
  U2 = Voltage Regulator - Variable [package="TO220 [THT]"]
  J2 = Basic Force Sensing Resistor (FSR) [package=THT]  # not connected
  T2 = LM35 Temperature Sensor [package="TO92 [THT]"]

nets:
  N1: Composant1.TXD, Composant2.D0/RX
  N2: Composant1.RXD, Composant2.D1/TX
  VCC: Composant1.VCC, Composant2.3V3
  GND: Composant1.GND, Composant2.GND
  N3: Composant2.A0, T1.Vout
  N4: Composant2.A1, T2.Vout
  N5: Composant2.D8, U1.input_voltage
  N6: Composant2.D9_PWM, U2.ADJ
  N7: Composant2.VIN, J1.pin_0
  N8: U1.GND, J1.pin_1
