# Fritzing sketch projet valabre (saved by Fritzing 0.9.3b)
perfboards: 1

parts:
  Composant1 = Arduino Nano (Rev3.0) (ICSP)
  U1 = LCD-16X2 [package=lcd-16x2]
  R1 = Trimmer Potentiometer [maximum_resistance=10kΩ package=THT]
  R2 = Resistor [tolerance=±5% resistance=220 package="1206 [SMD]"]
  Composant2 = Bluetooth HC-05 Macho
  LED1 = smd LED [color="Red (633nm)" package="1206 [SMD]"]
  R3 = Resistor [tolerance=±5% resistance=220 package="1206 [SMD]"]
  VCC1 = Battery
  S1 = SPST Switch [package=r_sw_th]
  J1 = Piezo Speaker

nets:
  N1: Composant1.D1/TX, Composant2.RXD
  N2: Composant1.D0/RX, Composant2.TXD
  N3: Composant1.GND, VCC1.-
  N4: Composant1.D2, U1.DB7
  N5: Composant1.D3, U1.DB6
  N6: Composant1.D4, U1.DB5
  N7: Composant1.D5, U1.DB4
  N8: Composant1.D8, J1.pin2
  N9: Composant1.D10, LED1.anode
  N10: Composant1.D11/MOSI, U1.E
  N11: Composant1.D12/MISO, U1.RS
  N12: Composant1.VIN, S1.O
  5V: Composant1.5V, U1.VDD
  3V3: Composant1.3V3, Composant2.VCC
  N13: U1.VO, R1.wiper
  N14: U1.A, R2.Pin_1
  N15: Composant2.GND, R3.Pin_0, J1.pin1
  N16: LED1.cathode, R3.Pin_1
